// Logisim project mips-like.circ as structural Verilog
module PROCESSADOR (
  output [31:0] \SAÍDA ,
  output [31:0] \INSTRUÇÃO ,
  output [31:0] \INSTRUÇÃO_2 
);

  wire and_1_out, branch, CLK, \escrever_na_memória , imediato, jump, \ler_da_memória , menor, or_1_out, RST,
       uc_v3_1_escrever_reg, uso_ula;
  wire [3:0] uc_v3_1_ula_op;
  wire [15:0] bit_extender_3_out;
  wire [31:0] adder_1_out, banco_de_registradores_1_r0_d, banco_de_registradores_1_r1_d, imediato_ULA,
       multiplexer_1_out, multiplexer_2_out, multiplexer_3_out, multiplexer_4_out, PC_q, ula_1_ula_out;

  Adder #(.width(32)) adder_1 (.a(PC_q), .b(32'h4), .out(adder_1_out));  // open: cin, cout
  Multiplexer #(.width(32)) multiplexer_1 (
    .in0(adder_1_out), .in1(\INSTRUÇÃO_2 ), .out(multiplexer_1_out), .sel(or_1_out));  // open: en
  or or_1 (or_1_out, jump, and_1_out);
  Clock clock_1 (.out(CLK));
  Button button_1 (.out(RST));
  Register #(.width(32)) PC (.D(multiplexer_1_out), .Q(PC_q), .clk(CLK), .clr(RST));  // open: en
  and and_1 (and_1_out, branch, menor);
  ROM #(.dataWidth(32)) rom_1 (.addr(PC_q[9:2]), .data(\INSTRUÇÃO ));  // open: sel
  Register register_1 ();  // open: D, en, Q, clk, clr
  uc_v3 uc_v3_1 (
    .E3(\INSTRUÇÃO [31]), .E2(\INSTRUÇÃO [30]), .E1(\INSTRUÇÃO [29]), .E0(\INSTRUÇÃO [28]),
    .ula_op(uc_v3_1_ula_op), .uso_ula(uso_ula), .escrever_reg(uc_v3_1_escrever_reg),
    .escrever_mem(\escrever_na_memória ), .jump(jump), .branch(branch), .ler_mem(\ler_da_memória ),
    .imediato(imediato));
  assign \INSTRUÇÃO_2  = {{8{1'b0}}, \INSTRUÇÃO [23:0]};  // Bit_Extender bit_extender_1
  assign imediato_ULA = {{12{1'b0}}, \INSTRUÇÃO [19:0]};  // Bit_Extender bit_extender_2
  BANCO_DE_REGISTRADORES banco_de_registradores_1 (
    .DATA_WRITE(multiplexer_2_out), .R0_D(banco_de_registradores_1_r0_d),
    .R1_D(banco_de_registradores_1_r1_d), .R0(\INSTRUÇÃO [19:16]), .R1(\INSTRUÇÃO [23:20]), .CLK(CLK),
    .RW_2(\INSTRUÇÃO [27:24]), .RW(uc_v3_1_escrever_reg), .RESET(RST));
  Multiplexer #(.width(32), .enable("false")) multiplexer_2 (
    .in0(multiplexer_3_out), .in1(\SAÍDA ), .out(multiplexer_2_out), .sel(\ler_da_memória ));
  Multiplexer #(.width(32), .enable("false")) multiplexer_3 (
    .in0(\INSTRUÇÃO_2 ), .in1(ula_1_ula_out), .out(multiplexer_3_out), .sel(uso_ula));
  Bit_Extender #(.in_width(32)) bit_extender_3 (.in(banco_de_registradores_1_r1_d), .out(bit_extender_3_out));
  Multiplexer #(.width(32), .enable("false")) multiplexer_4 (
    .in0(banco_de_registradores_1_r0_d), .in1(imediato_ULA), .out(multiplexer_4_out), .sel(imediato));
  Register register_2 ();  // open: D, en, Q, clk, clr
  ULA ula_1 (
    .DATA_0(multiplexer_4_out), .DATA_1(banco_de_registradores_1_r1_d), .ULA_OUT(ula_1_ula_out),
    .ULA_OP(uc_v3_1_ula_op), .menor(menor));
  RAM #(.addrWidth(16), .dataWidth(32), .bus("separate")) ram_1 (
    .addr(bit_extender_3_out), .din(multiplexer_4_out), .data(\SAÍDA ), .str(\escrever_na_memória ),
    .clk(CLK), .ld(\ler_da_memória ));  // open: sel, clr
  Register register_3 ();  // open: D, en, Q, clk, clr

  // Other names for the same wires on the sheet: saída_da_memória[31:0] = \SAÍDA ;
  //   valor_imediato[31:0] = \INSTRUÇÃO_2 

  // Notes on the sheet:
  //   add - 0, sub - 1, mul - 2, addi - 4
  //   j - 5, li - 6, lw - 7, sw - 8, sll - 9
  //   contents of rom_1 (hex, n*v repeats v):
  //   68000000 69000004 6a000008 60000000 61000000 62000000 63000000 6f000002 401f6666 62000000 402f0084
  //   63000000 64000000 2c1f0000 cc20000 cca0000 80c00000 403f0078 2d1f0000 dd30000 dd80000 76d00000
  //   2e3f0000 ee20000 ee90000 77e00000 2b670000 44b0000 33300001 50000044 80c40000 32200001 50000028
  //   31100001 50000020
  //   REG_0
  //   REG_1
  //   REG_W
  //   DATA_W
  //   REG0_D
  //   REG1_D
  //   ULA
endmodule

module ULA (
  input  [31:0] DATA_0,
  input  [31:0] DATA_1,
  input  [3:0] ULA_OP,
  output [31:0] ULA_OUT,
  output menor
);

  wire comparator_1_eq, comparator_1_gt, comparator_1_lt;
  wire [4:0] bit_extender_1_out;
  wire [31:0] adder_1_out, bit_extender_2_out, bit_extender_3_out, bit_extender_4_out, multiplier_1_out,
       shifter_1_out, shifter_2_out, subtractor_1_out;

  Bit_Extender #(.in_width(32), .out_width(5)) bit_extender_1 (.in(DATA_0), .out(bit_extender_1_out));
  Adder #(.width(32)) adder_1 (.a(DATA_0), .b(DATA_1), .out(adder_1_out));  // open: cin, cout
  Subtractor #(.width(32)) subtractor_1 (.a(DATA_0), .b(DATA_1), .out(subtractor_1_out));  // open: bin, bout
  Multiplier #(.width(32)) multiplier_1 (.a(DATA_0), .b(DATA_1), .out(multiplier_1_out));  // open: cin, cout
  Comparator #(.width(32), .mode("unsigned")) comparator_1 (
    .a(DATA_1), .b(DATA_0), .gt(comparator_1_gt), .eq(comparator_1_eq), .lt(comparator_1_lt));
  Shifter #(.width(32)) shifter_1 (.in(DATA_1), .\dist (bit_extender_1_out), .out(shifter_1_out));
  Shifter #(.width(32), .shift("lr")) shifter_2 (.in(DATA_1), .\dist (bit_extender_1_out), .out(shifter_2_out));
  assign bit_extender_2_out = {{31{1'b0}}, comparator_1_gt};  // Bit_Extender bit_extender_2
  assign bit_extender_3_out = {{31{1'b0}}, comparator_1_eq};  // Bit_Extender bit_extender_3
  assign bit_extender_4_out = {{31{1'b0}}, comparator_1_lt};  // Bit_Extender bit_extender_4
  Multiplexer #(.select(4), .width(32)) multiplexer_1 (
    .in0(adder_1_out), .in1(subtractor_1_out), .in2(multiplier_1_out), .in3(bit_extender_2_out),
    .in4(bit_extender_3_out), .in5(bit_extender_4_out), .in6(shifter_1_out), .in7(shifter_2_out),
    .out(ULA_OUT), .sel(ULA_OP));  // open: in8, in9, in10, in11, in12, in13, in14, in15, en
  not not_1 (menor, comparator_1_lt);

  // Notes on the sheet:
  //   sll
  //   slr
endmodule

module UC (
  input  E0,
  input  E1,
  input  E2,
  input  E3,
  output ula_op,
  output write_reg
);

  wire and_1_out, and_2_out, not_1_out, not_2_out, not_3_out, not_4_out, not_5_out, not_6_out, not_7_out,
       not_8_out, not_9_out;

  not not_1 (not_1_out, E0);
  not not_2 (not_2_out, E1);
  not not_3 (not_3_out, E2);
  not not_4 (not_4_out, E0);
  and and_1 (and_1_out, not_4_out, not_5_out, not_6_out);
  not not_5 (not_5_out, E1);
  not not_6 (not_6_out, E2);
  not not_7 (not_7_out, E0);
  and and_2 (and_2_out, not_7_out, not_8_out, not_9_out);
  not not_8 (not_8_out, E1);
  not not_9 (not_9_out, E3);
  and and_3 (ula_op, not_1_out, not_2_out, not_3_out, E3);
  or or_1 (write_reg, and_1_out, and_2_out);
endmodule

module BANCO_DE_REGISTRADORES (
  input  [31:0] DATA_WRITE,
  input  CLK,
  input  RESET,
  input  RW,
  input  [3:0] R0,
  input  [3:0] RW_2,
  input  [3:0] R1,
  output [31:0] R0_D,
  output [31:0] R1_D
);

  wire _0000w, _0001w, _0010w, _0011w, _0100w, _0101w, _0110w, _0111w, _1000w, _1001w, _1010w, _1011w,
       _1100w, _1101w, _1110w, _1111w;
  wire [31:0] _0000, _0001, _0010, _0011, _0100, _0101, _0110, _0111, _1000, _1001, _1010, _1011, _1100,
       _1101, _1110, _1111;

  Multiplexer #(.select(4), .width(32), .disabled(0), .enable("false")) multiplexer_1 (
    .in0(_0000), .in1(_0001), .in2(_0010), .in3(_0011), .in4(_0100), .in5(_0101), .in6(_0110), .in7(_0111),
    .in8(_1000), .in9(_1001), .in10(_1010), .in11(_1011), .in12(_1100), .in13(_1101), .in14(_1110),
    .in15(_1111), .out(R0_D), .sel(R0));
  Multiplexer #(.select(4), .width(32), .disabled(0), .enable("false")) multiplexer_2 (
    .in0(_0000), .in1(_0001), .in2(_0010), .in3(_0011), .in4(_0100), .in5(_0101), .in6(_0110), .in7(_0111),
    .in8(_1000), .in9(_1001), .in10(_1010), .in11(_1011), .in12(_1100), .in13(_1101), .in14(_1110),
    .in15(_1111), .out(R1_D), .sel(R1));
  Register #(.width(32)) register_1 (.D(DATA_WRITE), .en(_0000w), .Q(_0000), .clk(CLK), .clr(RESET));
  Register #(.width(32)) register_2 (.D(DATA_WRITE), .en(_0001w), .Q(_0001), .clk(CLK), .clr(RESET));
  Register #(.width(32)) register_3 (.D(DATA_WRITE), .en(_0010w), .Q(_0010), .clk(CLK), .clr(RESET));
  Register #(.width(32)) register_4 (.D(DATA_WRITE), .en(_0011w), .Q(_0011), .clk(CLK), .clr(RESET));
  Register #(.width(32)) register_5 (.D(DATA_WRITE), .en(_0100w), .Q(_0100), .clk(CLK), .clr(RESET));
  Register #(.width(32)) register_6 (.D(DATA_WRITE), .en(_0101w), .Q(_0101), .clk(CLK), .clr(RESET));
  Register #(.width(32)) register_7 (.D(DATA_WRITE), .en(_0110w), .Q(_0110), .clk(CLK), .clr(RESET));
  Register #(.width(32)) register_8 (.D(DATA_WRITE), .en(_0111w), .Q(_0111), .clk(CLK), .clr(RESET));
  Register #(.width(32)) register_9 (.D(DATA_WRITE), .en(_1000w), .Q(_1000), .clk(CLK), .clr(RESET));
  Register #(.width(32)) register_10 (.D(DATA_WRITE), .en(_1001w), .Q(_1001), .clk(CLK), .clr(RESET));
  Register #(.width(32)) register_11 (.D(DATA_WRITE), .en(_1010w), .Q(_1010), .clk(CLK), .clr(RESET));
  Register #(.width(32)) register_12 (.D(DATA_WRITE), .en(_1011w), .Q(_1011), .clk(CLK), .clr(RESET));
  Demultiplexer #(.select(4)) demultiplexer_1 (
    .out0(_0000w), .out1(_0001w), .out2(_0010w), .out3(_0011w), .out4(_0100w), .out5(_0101w), .out6(_0110w),
    .out7(_0111w), .out8(_1000w), .out9(_1001w), .out10(_1010w), .out11(_1011w), .out12(_1100w),
    .out13(_1101w), .out14(_1110w), .out15(_1111w), .in(RW), .sel(RW_2));  // open: en
  Register #(.width(32)) register_13 (.D(DATA_WRITE), .en(_1100w), .Q(_1100), .clk(CLK), .clr(RESET));
  Register #(.width(32)) register_14 (.D(DATA_WRITE), .en(_1101w), .Q(_1101), .clk(CLK), .clr(RESET));
  Register #(.width(32)) register_15 (.D(DATA_WRITE), .en(_1110w), .Q(_1110), .clk(CLK), .clr(RESET));
  Register #(.width(32)) register_16 (.D(DATA_WRITE), .en(_1111w), .Q(_1111), .clk(CLK), .clr(RESET));

  // Other names for the same wires on the sheet: write_c[31:0] = DATA_WRITE
endmodule

module uc_control (
  input  E0,
  input  E1,
  input  E2,
  input  E3,
  output [3:0] ula_op,
  output escrever_reg,
  output escrever_mem,
  output jump,
  output branch,
  output reg_mem,
  output ler_mem
);

  wire and_1_out, and_2_out, and_3_out, and_4_out, not_1_out, not_2_out, not_3_out, not_4_out, not_5_out,
       not_6_out, not_7_out, not_8_out, not_9_out, not_10_out, not_11_out, not_12_out, not_13_out,
       not_14_out, not_15_out, not_16_out, not_17_out, not_18_out, not_19_out, not_20_out, not_21_out;

  not not_1 (not_1_out, E0);
  and and_1 (and_1_out, not_1_out, not_2_out);
  not not_2 (not_2_out, E1);
  not not_3 (not_3_out, E0);
  not not_4 (not_4_out, E2);
  and and_2 (and_2_out, not_3_out, not_4_out, not_5_out);
  not not_5 (not_5_out, E3);
  not not_6 (not_6_out, E1);
  not not_7 (not_7_out, E2);
  and and_3 (and_3_out, not_6_out, not_7_out, not_8_out);
  not not_8 (not_8_out, E3);
  not not_9 (not_9_out, E0);
  and and_4 (and_4_out, not_9_out, E2, E3);
  not not_10 (not_10_out, E1);
  not not_11 (not_11_out, E2);
  not not_12 (not_12_out, E3);
  not not_13 (not_13_out, E0);
  not not_14 (not_14_out, E2);
  not not_15 (not_15_out, E0);
  not not_16 (not_16_out, E3);
  not not_17 (not_17_out, E1);
  not not_18 (not_18_out, E2);
  not not_19 (not_19_out, E3);
  not not_20 (not_20_out, E1);
  not not_21 (not_21_out, E2);
  or or_1 (escrever_reg, and_1_out, and_2_out, and_3_out, and_4_out);
  and and_5 (escrever_mem, E0, not_10_out, not_11_out, not_12_out);
  and and_6 (jump, not_13_out, E1, not_14_out, E3);
  and and_7 (branch, not_15_out, E1, E2, not_16_out);
  and and_8 (reg_mem, E0, not_17_out, not_18_out, not_19_out);
  and and_9 (ler_mem, E0, not_20_out, not_21_out, E3);

  assign ula_op = {E0, E1, E2, E3};
endmodule

module uc_v2 (
  input  E3,
  input  E2,
  input  E1,
  input  E0,
  output [3:0] ula_op,
  output escrever_reg,
  output escrever_mem,
  output jump,
  output branch,
  output reg_para_mem,
  output ler_mem,
  output imediato
);

  wire and_3_out, and_4_out, and_5_out, and_6_out, and_7_out, and_13_out, and_14_out, not_1_out, not_2_out,
       not_3_out, not_4_out, not_5_out, not_6_out, not_7_out, not_8_out, not_9_out, not_10_out, not_11_out,
       not_12_out, not_13_out, not_14_out, not_15_out, not_16_out, not_17_out, not_18_out, not_19_out,
       not_20_out, not_21_out, not_22_out, not_23_out, not_24_out, not_25_out, not_26_out;

  and and_1 (ula_op[2], E2, not_1_out);
  not not_1 (not_1_out, E0);
  and and_2 (ula_op[1], E1, not_2_out);
  not not_2 (not_2_out, E0);
  not not_3 (not_3_out, E2);
  and and_3 (and_3_out, not_3_out, not_4_out, E0);
  not not_4 (not_4_out, E1);
  and and_4 (and_4_out, E2, not_5_out);
  not not_5 (not_5_out, E0);
  not not_6 (not_6_out, E3);
  and and_5 (and_5_out, not_6_out, not_7_out, not_8_out);
  not not_7 (not_7_out, E2);
  not not_8 (not_8_out, E1);
  not not_9 (not_9_out, E2);
  not not_10 (not_10_out, E1);
  and and_6 (and_6_out, not_9_out, not_10_out, E0);
  not not_11 (not_11_out, E3);
  and and_7 (and_7_out, not_11_out, E2, E1);
  not not_12 (not_12_out, E2);
  not not_13 (not_13_out, E1);
  not not_14 (not_14_out, E0);
  not not_15 (not_15_out, E3);
  not not_16 (not_16_out, E1);
  not not_17 (not_17_out, E3);
  not not_18 (not_18_out, E1);
  not not_19 (not_19_out, E0);
  not not_20 (not_20_out, E2);
  and and_8 (reg_para_mem, E3, not_20_out, not_21_out);
  not not_21 (not_21_out, E1);
  not not_22 (not_22_out, E3);
  not not_23 (not_23_out, E3);
  not not_24 (not_24_out, E2);
  not not_25 (not_25_out, E3);
  not not_26 (not_26_out, E0);
  or or_1 (ula_op[0], and_3_out, and_4_out, E3);
  or or_2 (escrever_reg, and_5_out, and_6_out, and_7_out);
  and and_9 (escrever_mem, E3, not_12_out, not_13_out, not_14_out);
  and and_10 (jump, not_15_out, E2, not_16_out, E0);
  and and_11 (branch, not_17_out, E2, not_18_out, not_19_out);
  and and_12 (ler_mem, not_22_out, E2, E1, E0);
  and and_13 (and_13_out, not_23_out, not_24_out, E1, E0);
  or or_3 (imediato, and_13_out, and_14_out);
  and and_14 (and_14_out, not_25_out, E2, E1, not_26_out);

  assign ula_op[3] = 1'b0;
endmodule

module uc_v3 (
  input  E3,
  input  E2,
  input  E1,
  input  E0,
  output [3:0] ula_op,
  output uso_ula,
  output escrever_reg,
  output escrever_mem,
  output jump,
  output branch,
  output ler_mem,
  output imediato
);

  wire and_1_out, and_2_out, and_3_out, and_4_out, and_5_out, and_6_out, and_7_out, and_9_out, and_10_out,
       and_11_out, and_12_out, and_13_out, not_1_out, not_2_out, not_3_out, not_4_out, not_5_out, not_6_out,
       not_7_out, not_8_out, not_9_out, not_10_out, not_11_out, not_12_out, not_13_out, not_14_out,
       not_15_out, not_16_out, not_17_out, not_18_out, not_19_out, not_20_out, not_21_out, not_22_out,
       not_23_out, not_24_out, not_25_out, not_26_out, not_27_out;

  and and_1 (and_1_out, E2, not_1_out);
  not not_1 (not_1_out, E0);
  and and_2 (and_2_out, E1, not_2_out);
  not not_2 (not_2_out, E0);
  not not_3 (not_3_out, E3);
  not not_4 (not_4_out, E2);
  not not_5 (not_5_out, E1);
  not not_6 (not_6_out, E0);
  not not_7 (not_7_out, E3);
  and and_3 (and_3_out, not_7_out, not_8_out);
  not not_8 (not_8_out, E2);
  not not_9 (not_9_out, E3);
  and and_4 (and_4_out, not_9_out, not_10_out, not_11_out);
  not not_10 (not_10_out, E1);
  not not_11 (not_11_out, E0);
  not not_12 (not_12_out, E2);
  and and_5 (and_5_out, not_12_out, E0);
  not not_13 (not_13_out, E3);
  and and_6 (and_6_out, not_13_out, not_14_out);
  not not_14 (not_14_out, E2);
  not not_15 (not_15_out, E2);
  and and_7 (and_7_out, not_15_out, E0);
  not not_16 (not_16_out, E2);
  not not_17 (not_17_out, E1);
  not not_18 (not_18_out, E0);
  not not_19 (not_19_out, E3);
  not not_20 (not_20_out, E1);
  not not_21 (not_21_out, E3);
  not not_22 (not_22_out, E1);
  not not_23 (not_23_out, E0);
  // AND_Gate and_8 has open pins: in0=E3, in1=not_24_out, out=open
  not not_24 (not_24_out, E0);
  not not_25 (not_25_out, E3);
  not not_26 (not_26_out, E2);
  and and_9 (and_9_out, not_26_out, E1, E0);
  and and_10 (and_10_out, E2, E1, not_27_out);
  not not_27 (not_27_out, E0);
  and and_11 (and_11_out, E3, E0);
  or or_1 (ula_op[2], and_1_out, E3);
  or or_2 (ula_op[1], and_2_out, E3);
  and and_12 (and_12_out, not_3_out, not_4_out, not_5_out, E0);
  or or_3 (ula_op[0], and_12_out, and_13_out);
  and and_13 (and_13_out, E2, not_6_out);
  or or_4 (uso_ula, and_3_out, and_4_out, and_5_out);
  or or_5 (escrever_reg, and_6_out, and_7_out, E1);
  and and_14 (escrever_mem, E3, not_16_out, not_17_out, not_18_out);
  and and_15 (jump, not_19_out, E2, not_20_out, E0);
  and and_16 (branch, not_21_out, E2, not_22_out, not_23_out);
  and and_17 (ler_mem, not_25_out, E2, E1, E0);
  or or_6 (imediato, and_9_out, and_10_out, and_11_out);

  assign ula_op[3] = 1'b0;
endmodule

module memoria_aux (
  input  [7:0] Mem_adr,
  input  [31:0] AUX_1,
  output [7:0] out_3
);

  wire [31:0] adder_1_out, bit_extender_1_out;

  assign bit_extender_1_out = {{24{1'b0}}, Mem_adr};  // Bit_Extender bit_extender_1
  Adder #(.width(32)) adder_1 (.a(bit_extender_1_out), .b(AUX_1), .out(adder_1_out));  // open: cin, cout
  Bit_Extender #(.in_width(32), .out_width(8)) bit_extender_2 (.in(adder_1_out), .out(out_3));
endmodule
