// Logisim project processadorPipeline.circ as structural Verilog: 4 circuits, main circuit PROCESSADOR
module PROCESSADOR (
  input  in_1,
  output [31:0] \SAÍDA ,
  output [31:0] \INSTRUÇÃO ,
  output [7:0] \INSTRUÇÃO_2 ,
  output [31:0] \INSTRUÇÃO_3 ,
  output [31:0] \INSTRUÇÃO_4 
);

  wire and_1_out, branch, button_1_out, CLK, \escrever_na_memória , escrever_no_BR, imediato, jump,
       \ler_da_memória , menor, or_1_out, register_1_q, register_4_q, register_7_q, ula_1_menor, usar_ULA;
  wire [3:0] REG_W1, register_3_q, register_11_q, uc_1_ula_op;
  wire [5:1] register_10_q;
  wire [6:0] uc_1_uso_ula;
  wire [15:0] bit_extender_3_out, register_17_q;
  wire [31:0] adder_1_out, banco_de_registradores_1_r0_d, banco_de_registradores_1_r1_d, bit_extender_1_out,
       bit_extender_2_out, imediato_ULA, multiplexer_1_out, multiplexer_2_out, multiplexer_3_out,
       multiplexer_4_out, register_6_q, register_12_q, register_13_q, register_18_q, register_20_q,
       rom_1_data, ula_1_ula_out;

  Adder #(.width(32)) adder_1 (
    .a({\INSTRUÇÃO_4 [31:10], \INSTRUÇÃO_2 , \INSTRUÇÃO_4 [1:0]}), .b(32'h4), .out(adder_1_out));  // open: cin, cout
  Multiplexer #(.width(32)) multiplexer_1 (
    .in0(adder_1_out), .in1(\INSTRUÇÃO_3 ), .out(multiplexer_1_out), .sel(or_1_out));  // open: en
  or or_1 (or_1_out, register_1_q, and_1_out);
  Register #(.width(1)) register_1 (.D(jump), .Q(register_1_q), .clk(CLK), .clr(in_1));  // open: en
  Register #(.width(32)) PC (
    .D(multiplexer_1_out), .Q({\INSTRUÇÃO_4 [31:10], \INSTRUÇÃO_2 , \INSTRUÇÃO_4 [1:0]}), .clk(CLK),
    .clr(in_1));  // open: en
  and and_1 (and_1_out, register_4_q, menor);
  ROM #(.dataWidth(32)) rom_1 (.addr(\INSTRUÇÃO_2 ), .data(rom_1_data));  // open: sel
  Register #(.width(4)) register_2 (.D(register_3_q), .Q(REG_W1), .clk(CLK), .clr(in_1));  // open: en
  Register #(.width(4)) register_3 (.D(\INSTRUÇÃO [27:24]), .Q(register_3_q), .clk(CLK), .clr(in_1));  // open: en
  Register #(.width(1)) register_4 (.D(branch), .Q(register_4_q), .clk(CLK), .clr(in_1));  // open: en
  Register #(.width(32)) register_5 (.D(rom_1_data), .Q(\INSTRUÇÃO ), .clk(CLK), .clr(in_1));  // open: en
  UC uc_1 (
    .E3(\INSTRUÇÃO [31]), .E2(\INSTRUÇÃO [30]), .E1(\INSTRUÇÃO [29]), .E0(\INSTRUÇÃO [28]),
    .ula_op(uc_1_ula_op), .uso_ula(uc_1_uso_ula[0]), .escrever_reg(uc_1_uso_ula[1]),
    .escrever_mem(uc_1_uso_ula[2]), .jump(uc_1_uso_ula[3]), .branch(uc_1_uso_ula[4]),
    .ler_mem(uc_1_uso_ula[5]), .imediato(uc_1_uso_ula[6]));
  Register #(.width(32)) register_6 (.D(bit_extender_1_out), .Q(register_6_q), .clk(CLK), .clr(in_1));  // open: en
  assign bit_extender_1_out = {{16{1'b0}}, \INSTRUÇÃO [15:0]};  // Bit_Extender bit_extender_1
  assign bit_extender_2_out = {{12{1'b0}}, \INSTRUÇÃO [19:0]};  // Bit_Extender bit_extender_2
  BANCO_DE_REGISTRADORES banco_de_registradores_1 (
    .DATA_WRITE(multiplexer_3_out), .R0_D(banco_de_registradores_1_r0_d),
    .R1_D(banco_de_registradores_1_r1_d), .R0(\INSTRUÇÃO [19:16]), .R1(\INSTRUÇÃO [23:20]), .CLK(CLK),
    .RW_2(REG_W1), .RW(escrever_no_BR), .RESET(in_1));
  Multiplexer #(.width(32), .enable("false")) multiplexer_2 (
    .in0(\INSTRUÇÃO_3 ), .in1(register_20_q), .out(multiplexer_2_out), .sel(register_7_q));
  Register #(.width(1)) register_7 (.D(usar_ULA), .Q(register_7_q), .clk(CLK), .clr(in_1));  // open: en
  Register #(.width(32)) register_8 (.D(bit_extender_2_out), .Q(imediato_ULA), .clk(CLK), .clr(in_1));  // open: en
  Multiplexer #(.width(32), .enable("false")) multiplexer_3 (
    .in0(multiplexer_2_out), .in1(\SAÍDA ), .out(multiplexer_3_out), .sel(\ler_da_memória ));
  Register #(.width(32)) register_9 (.D(register_6_q), .Q(\INSTRUÇÃO_3 ), .clk(CLK), .clr(in_1));  // open: en
  Register #(.width(7)) register_10 (
    .D(uc_1_uso_ula), .Q({imediato, register_10_q[5], branch, jump, register_10_q[2:1], usar_ULA}),
    .clk(CLK), .clr(in_1));  // open: en
  Register #(.width(4)) register_11 (.D(uc_1_ula_op), .Q(register_11_q), .clk(CLK), .clr(in_1));  // open: en
  Register #(.width(32)) register_12 (
    .D(banco_de_registradores_1_r0_d), .Q(register_12_q), .clk(CLK), .clr(in_1));  // open: en
  Register #(.width(32)) register_13 (
    .D(banco_de_registradores_1_r1_d), .Q(register_13_q), .clk(CLK), .clr(in_1));  // open: en
  Register #(.width(1)) register_14 (.D(register_10_q[1]), .Q(escrever_no_BR), .clk(CLK), .clr(in_1));  // open: en
  Register #(.width(1)) register_15 (
    .D(register_10_q[2]), .Q(\escrever_na_memória ), .clk(CLK), .clr(in_1));  // open: en
  Register #(.width(1)) register_16 (.D(register_10_q[5]), .Q(\ler_da_memória ), .clk(CLK), .clr(in_1));  // open: en
  Multiplexer #(.width(32), .enable("false")) multiplexer_4 (
    .in0(register_12_q), .in1(imediato_ULA), .out(multiplexer_4_out), .sel(imediato));
  Bit_Extender #(.in_width(32)) bit_extender_3 (.in(register_13_q), .out(bit_extender_3_out));
  Clock clock_1 (.out(CLK));
  Register #(.width(16)) register_17 (.D(bit_extender_3_out), .Q(register_17_q), .clk(CLK), .clr(in_1));  // open: en
  Register #(.width(32)) register_18 (.D(multiplexer_4_out), .Q(register_18_q), .clk(CLK), .clr(in_1));  // open: en
  ULA ula_1 (
    .DATA_0(multiplexer_4_out), .DATA_1(register_13_q), .ULA_OUT(ula_1_ula_out), .ULA_OP(register_11_q),
    .menor(ula_1_menor));
  Register #(.width(1)) register_19 (.D(ula_1_menor), .Q(menor), .clk(CLK), .clr(in_1));  // open: en
  Register #(.width(32)) register_20 (.D(ula_1_ula_out), .Q(register_20_q), .clk(CLK), .clr(in_1));  // open: en
  RAM #(.addrWidth(16), .dataWidth(32), .bus("separate")) ram_1 (
    .addr(register_17_q), .din(register_18_q), .data(\SAÍDA ), .str(\escrever_na_memória ), .clk(CLK),
    .ld(\ler_da_memória ), .clr(button_1_out));  // open: sel
  Button button_1 (.out(button_1_out));

  assign \INSTRUÇÃO_4 [9:2] = \INSTRUÇÃO_2 ;

  // Other names for the same wires on the sheet: REG_W[3:0] = \INSTRUÇÃO [27:24]; RST = in_1;
  //   saída_da_memória[31:0] = \SAÍDA ; valor_imediato[31:0] = \INSTRUÇÃO_3 

  // Notes on the sheet:
  //   add - 0, sub - 1, mul - 2, addi - 4
  //   j - 5, li - 6, lw - 7, sw - 8, sll - 9
  //   contents of rom_1 (hex, n*v repeats v):
  //   68000000 69000004 6a000008 60000000 61000000 62000000 63000000 6f000002 4*0 401f0300 4*0 62000000
  //   4*0 402f0224 4*0 63000000 4*0 64000000 4*0 2c1f0000 4*0 cc20000 4*0 cca0000 4*0 80c00000 4*0
  //   403f01e8 4*0 2d1f0000 4*0 dd30000 4*0 dd80000 4*0 76d00000 4*0 2e3f0000 4*0 ee20000 4*0 ee90000 4*0
  //   77e00000 4*0 2b670000 4*0 44b0000 4*0 33300001 4*0 500000e4 4*0 80c40000 4*0 32200001 4*0 50000058
  //   4*0 31100001 4*0 50000030
  //   IF/ID
  //   REG_0
  //   REG_1
  //   REG_W
  //   DATA_W
  //   REG0_D
  //   REG1_D
  //   ULA
  //   resetar memória?
endmodule

module BANCO_DE_REGISTRADORES (
  input  [31:0] DATA_WRITE,
  input  CLK,
  input  RESET,
  input  RW,
  input  [3:0] R0,
  input  [3:0] RW_2,
  input  [3:0] R1,
  output [31:0] R0_D,
  output [31:0] R1_D
);

  wire _0000w, _0001w, _0010w, _0011w, _0100w, _0101w, _0110w, _0111w, _1000w, _1001w, _1010w, _1011w,
       _1100w, _1101w, _1110w, _1111w;
  wire [31:0] _0000, _0001, _0010, _0011, _0100, _0101, _0110, _0111, _1000, _1001, _1010, _1011, _1100,
       _1101, _1110, _1111;

  Multiplexer #(.select(4), .width(32), .disabled(0), .enable("false")) multiplexer_1 (
    .in0(_0000), .in1(_0001), .in2(_0010), .in3(_0011), .in4(_0100), .in5(_0101), .in6(_0110), .in7(_0111),
    .in8(_1000), .in9(_1001), .in10(_1010), .in11(_1011), .in12(_1100), .in13(_1101), .in14(_1110),
    .in15(_1111), .out(R0_D), .sel(R0));
  Multiplexer #(.select(4), .width(32), .disabled(0), .enable("false")) multiplexer_2 (
    .in0(_0000), .in1(_0001), .in2(_0010), .in3(_0011), .in4(_0100), .in5(_0101), .in6(_0110), .in7(_0111),
    .in8(_1000), .in9(_1001), .in10(_1010), .in11(_1011), .in12(_1100), .in13(_1101), .in14(_1110),
    .in15(_1111), .out(R1_D), .sel(R1));
  Register #(.width(32)) register_1 (.D(DATA_WRITE), .en(_0000w), .Q(_0000), .clk(CLK), .clr(RESET));
  Register #(.width(32)) register_2 (.D(DATA_WRITE), .en(_0001w), .Q(_0001), .clk(CLK), .clr(RESET));
  Register #(.width(32)) register_3 (.D(DATA_WRITE), .en(_0010w), .Q(_0010), .clk(CLK), .clr(RESET));
  Register #(.width(32)) register_4 (.D(DATA_WRITE), .en(_0011w), .Q(_0011), .clk(CLK), .clr(RESET));
  Register #(.width(32)) register_5 (.D(DATA_WRITE), .en(_0100w), .Q(_0100), .clk(CLK), .clr(RESET));
  Register #(.width(32)) register_6 (.D(DATA_WRITE), .en(_0101w), .Q(_0101), .clk(CLK), .clr(RESET));
  Register #(.width(32)) register_7 (.D(DATA_WRITE), .en(_0110w), .Q(_0110), .clk(CLK), .clr(RESET));
  Register #(.width(32)) register_8 (.D(DATA_WRITE), .en(_0111w), .Q(_0111), .clk(CLK), .clr(RESET));
  Register #(.width(32)) register_9 (.D(DATA_WRITE), .en(_1000w), .Q(_1000), .clk(CLK), .clr(RESET));
  Register #(.width(32)) register_10 (.D(DATA_WRITE), .en(_1001w), .Q(_1001), .clk(CLK), .clr(RESET));
  Register #(.width(32)) register_11 (.D(DATA_WRITE), .en(_1010w), .Q(_1010), .clk(CLK), .clr(RESET));
  Register #(.width(32)) register_12 (.D(DATA_WRITE), .en(_1011w), .Q(_1011), .clk(CLK), .clr(RESET));
  Demultiplexer #(.select(4)) demultiplexer_1 (
    .out0(_0000w), .out1(_0001w), .out2(_0010w), .out3(_0011w), .out4(_0100w), .out5(_0101w), .out6(_0110w),
    .out7(_0111w), .out8(_1000w), .out9(_1001w), .out10(_1010w), .out11(_1011w), .out12(_1100w),
    .out13(_1101w), .out14(_1110w), .out15(_1111w), .in(RW), .sel(RW_2));  // open: en
  Register #(.width(32)) register_13 (.D(DATA_WRITE), .en(_1100w), .Q(_1100), .clk(CLK), .clr(RESET));
  Register #(.width(32)) register_14 (.D(DATA_WRITE), .en(_1101w), .Q(_1101), .clk(CLK), .clr(RESET));
  Register #(.width(32)) register_15 (.D(DATA_WRITE), .en(_1110w), .Q(_1110), .clk(CLK), .clr(RESET));
  Register #(.width(32)) register_16 (.D(DATA_WRITE), .en(_1111w), .Q(_1111), .clk(CLK), .clr(RESET));

  // Other names for the same wires on the sheet: write_c[31:0] = DATA_WRITE

  // Notes on the sheet:
  //   1 2
  //   3 4
  //   5 6
  //   7 8
endmodule

module ULA (
  input  [31:0] DATA_0,
  input  [31:0] DATA_1,
  input  [3:0] ULA_OP,
  output [31:0] ULA_OUT,
  output menor
);

  wire comparator_1_eq, comparator_1_gt, comparator_1_lt;
  wire [4:0] bit_extender_1_out;
  wire [31:0] adder_1_out, bit_extender_2_out, bit_extender_3_out, bit_extender_4_out, multiplier_1_out,
       shifter_1_out, shifter_2_out, subtractor_1_out;

  Bit_Extender #(.in_width(32), .out_width(5)) bit_extender_1 (.in(DATA_0), .out(bit_extender_1_out));
  Adder #(.width(32)) adder_1 (.a(DATA_0), .b(DATA_1), .out(adder_1_out));  // open: cin, cout
  Subtractor #(.width(32)) subtractor_1 (.a(DATA_0), .b(DATA_1), .out(subtractor_1_out));  // open: bin, bout
  Multiplier #(.width(32)) multiplier_1 (.a(DATA_0), .b(DATA_1), .out(multiplier_1_out));  // open: cin, cout
  Comparator #(.width(32), .mode("unsigned")) comparator_1 (
    .a(DATA_1), .b(DATA_0), .gt(comparator_1_gt), .eq(comparator_1_eq), .lt(comparator_1_lt));
  Shifter #(.width(32)) shifter_1 (.in(DATA_1), .\dist (bit_extender_1_out), .out(shifter_1_out));
  Shifter #(.width(32), .shift("lr")) shifter_2 (.in(DATA_1), .\dist (bit_extender_1_out), .out(shifter_2_out));
  assign bit_extender_2_out = {{31{1'b0}}, comparator_1_gt};  // Bit_Extender bit_extender_2
  assign bit_extender_3_out = {{31{1'b0}}, comparator_1_eq};  // Bit_Extender bit_extender_3
  assign bit_extender_4_out = {{31{1'b0}}, comparator_1_lt};  // Bit_Extender bit_extender_4
  Multiplexer #(.select(4), .width(32)) multiplexer_1 (
    .in0(adder_1_out), .in1(subtractor_1_out), .in2(multiplier_1_out), .in3(bit_extender_2_out),
    .in4(bit_extender_3_out), .in5(bit_extender_4_out), .in6(shifter_1_out), .in7(shifter_2_out),
    .out(ULA_OUT), .sel(ULA_OP));  // open: in8, in9, in10, in11, in12, in13, in14, in15, en
  not not_1 (menor, comparator_1_lt);

  // Notes on the sheet:
  //   SHAMT
  //   sll
  //   slr
endmodule

module UC (
  input  E3,
  input  E2,
  input  E1,
  input  E0,
  output [3:0] ula_op,
  output uso_ula,
  output escrever_reg,
  output escrever_mem,
  output jump,
  output branch,
  output ler_mem,
  output imediato
);

  wire and_1_out, and_2_out, and_3_out, and_4_out, and_5_out, and_6_out, and_7_out, and_9_out, and_10_out,
       and_11_out, and_12_out, and_13_out, not_1_out, not_2_out, not_3_out, not_4_out, not_5_out, not_6_out,
       not_7_out, not_8_out, not_9_out, not_10_out, not_11_out, not_12_out, not_13_out, not_14_out,
       not_15_out, not_16_out, not_17_out, not_18_out, not_19_out, not_20_out, not_21_out, not_22_out,
       not_23_out, not_24_out, not_25_out, not_26_out, not_27_out;

  and and_1 (and_1_out, E2, not_1_out);
  not not_1 (not_1_out, E0);
  and and_2 (and_2_out, E1, not_2_out);
  not not_2 (not_2_out, E0);
  not not_3 (not_3_out, E3);
  not not_4 (not_4_out, E2);
  not not_5 (not_5_out, E1);
  not not_6 (not_6_out, E0);
  not not_7 (not_7_out, E3);
  and and_3 (and_3_out, not_7_out, not_8_out);
  not not_8 (not_8_out, E2);
  not not_9 (not_9_out, E3);
  not not_10 (not_10_out, E1);
  and and_4 (and_4_out, not_9_out, not_10_out, not_11_out);
  not not_11 (not_11_out, E0);
  not not_12 (not_12_out, E2);
  and and_5 (and_5_out, not_12_out, E0);
  not not_13 (not_13_out, E3);
  and and_6 (and_6_out, not_13_out, not_14_out);
  not not_14 (not_14_out, E2);
  not not_15 (not_15_out, E2);
  and and_7 (and_7_out, not_15_out, E0);
  not not_16 (not_16_out, E2);
  not not_17 (not_17_out, E1);
  not not_18 (not_18_out, E0);
  not not_19 (not_19_out, E3);
  not not_20 (not_20_out, E1);
  not not_21 (not_21_out, E3);
  not not_22 (not_22_out, E1);
  not not_23 (not_23_out, E0);
  // AND_Gate and_8 has open pins: in0=E3, in1=not_24_out, out=open
  not not_24 (not_24_out, E0);
  not not_25 (not_25_out, E3);
  not not_26 (not_26_out, E2);
  and and_9 (and_9_out, not_26_out, E1, E0);
  and and_10 (and_10_out, E2, E1, not_27_out);
  not not_27 (not_27_out, E0);
  and and_11 (and_11_out, E3, E0);
  or or_1 (ula_op[2], and_1_out, E3);
  or or_2 (ula_op[1], and_2_out, E3);
  and and_12 (and_12_out, not_3_out, not_4_out, not_5_out, E0);
  or or_3 (ula_op[0], and_12_out, and_13_out);
  and and_13 (and_13_out, E2, not_6_out);
  or or_4 (uso_ula, and_3_out, and_4_out, and_5_out);
  or or_5 (escrever_reg, and_6_out, and_7_out, E1);
  and and_14 (escrever_mem, E3, not_16_out, not_17_out, not_18_out);
  and and_15 (jump, not_19_out, E2, not_20_out, E0);
  and and_16 (branch, not_21_out, E2, not_22_out, not_23_out);
  and and_17 (ler_mem, not_25_out, E2, E1, E0);
  or or_6 (imediato, and_9_out, and_10_out, and_11_out);

  assign ula_op[3] = 1'b0;
endmodule
